# Fritzing sketch ruka (saved by Fritzing 0.9.4)

parts:
  Part2 = Arduino Uno (Rev3) - ICSP
  Part3 = Adafruit PCA9685 PWM/Servo Breakout [part_number=815]
  SERVO1 = Tower Pro SG90 servo [part_number=101246]
  SERVO2 = Tower Pro SG90 servo [part_number=101246]
  SERVO3 = Tower Pro SG90 servo [part_number=101246]
  J2 = Basic Servo
  J4 = Basic Servo
  J5 = Basic Servo
  Part4 = Bluetooth HC-05 Macho  # not connected
  M1 = TP4056 Module [part_number=HW-107]
  VCC1 = Battery
  Boost_Convertor1 = Boost Convertor [part_number=XL6009E1 package=THT]

nets:
  N1: Part2.A4/SDA, Part3.SDA
  N2: Part2.A5/SCL, Part3.SCL
  GND: Part2.GND, Part3.GND, SERVO1.GND, SERVO2.GND, SERVO3.GND, J2.gnd, J4.gnd, J5.gnd, M1.OUT-#1, Boost_Convertor1.Negative_Output
  5V: Part2.5V, Part3.VCC
  N3: Part2.VIN, M1.OUT-#4
  N4: Part3.PWRIN, Boost_Convertor1.Positive_Output
  N5: Part3.PWM2, J5.pulse
  +5V: Part3.5.0V, SERVO1.+5V, SERVO2.+5V, SERVO3.+5V, J2.vcc, J4.vcc, J5.vcc
  N6: Part3.PWM1, J2.pulse
  N7: Part3.PWM0, J4.pulse
  N8: Part3.PWM15, SERVO3.Signal
  N9: Part3.PWM14, SERVO2.Signal
  N10: Part3.PWM13, SERVO1.Signal
  N11: M1.BAT-, VCC1.-, Boost_Convertor1.Negative_Input
  N12: M1.BAT+, VCC1.+, Boost_Convertor1.Positive_Input

custom parts:
  Adafruit PCA9685 PWM/Servo Breakout: Using only two pins, control 16 free-running PWM outputs! I2C-controlled PWM driver with a built in clock. Unlike the TLC5940 family, you do not need to continuously send it signal tying up your microcontroller, its completely free running! 5V compliant, which means you can control it from a 3.3V microcontroller and still safely drive up to 6V outputs (this is good for when you want to control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
  Tower Pro SG90 servo: Original file by John De Cristofaro http://www.adafruit.com/products/1449 Adafruit Feedback Servo (Small) Edited by: e-radionica.com 28/9/2015
  TP4056 Module: TP4056 Lithium Battery Charge Management Module Links: TP4056 website
  Battery: Your standard 2x 18650 battery pack (14.7 Volts)
  Boost Convertor: DC to DC boost convertor
